# Fritzing sketch Sismografo (saved by Fritzing 0.9.3b)
breadboards: 2

parts:
  U1 = ESP8266 WiFi Module [part_number=ESP8266]
  Componente1 = Arduino Mega 2560 (Rev3)-TopMount
  R1 = Resistor [tolerance=±5% resistance=220 package=THT]
  R2 = Resistor [tolerance=±5% resistance=220 package=THT]
  R3 = Resistor [tolerance=±5% resistance=220 package="2512 [SMD]"]
  R3_2 = Resistor [tolerance=±5% resistance=10k package="2010 [SMD]"]
  IC1 = DIP - 8 pins [part_number=LM741 package="DIP (Dual Inline) [THT]"]
  M1 = DC Motor
  R4 = Resistor [tolerance=±5% resistance=220 package=THT]
  R5 = Resistor [tolerance=±5% resistance=220 package=THT]
  LCD1 = 20x4 LCD display [part_number=2004A]

nets:
  N1: U1.RXD, R1.Pin_1, R2.Pin_1
  N2: U1.VCC, U1.CH_PD, R3.Pin_1, R3_2.Pin_1
  GND: U1.GND, Componente1.GND, R2.Pin_0, IC1.pin3, LCD1.Vss
  N3: U1.TXD, Componente1.D3_PWM
  N4: Componente1.A14, IC1.pin6, R5.Pin_1
  5V: Componente1.5V, R3.Pin_0, R3_2.Pin_0, IC1.pin7, LCD1.Vdd
  N5: Componente1.D2_PWM, R1.Pin_0
  N6: Componente1.D28, LCD1.A_+
  N7: Componente1.D31, LCD1.DB7
  N8: Componente1.D33, LCD1.DB6
  N9: Componente1.D35, LCD1.DB5
  N10: Componente1.D37, LCD1.DB4
  N11: Componente1.D39, LCD1.DB3
  N12: Componente1.D41, LCD1.DB2
  N13: Componente1.D43, LCD1.DB1
  N14: Componente1.D45, LCD1.DB0
  N15: Componente1.D47, LCD1.E
  N16: Componente1.D49, LCD1.R/W
  N17: Componente1.D51, LCD1.RS
  N18: Componente1.D53, LCD1.Vo
  N19: IC1.pin2, R4.Pin_1, R5.Pin_0
  N20: IC1.pin4, M1.pin_2
  N21: M1.pin_1, R4.Pin_0

custom parts:
  ESP8266 WiFi Module: Generic WiFi Module based on the ESP8266 with onboard PCB antenna and UART communications
  Arduino Mega 2560 (Rev3)-TopMount: Arduino Mega 2560 (Rev3) for Top PCB Mount. The PCB view of the Arduino Mega 2560 (Rev3) in Arduino Bin flipped upside down with the text flipped back so as to be readable. Other views haven't changed Protruding component position is outlined to provide indication of part contact. Number in component outline is mm of protrusion of the component from the Mega PCB. Subtract the number from the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
  DIP - 8 pins: A DIP stand-in part for whatever IC you want. With 8 pins on a 300 mil dual inline package (DIP) footprint.
  20x4 LCD display: 20x4 character display. CHECK LED POLARITY BEFORE CONNECTING POWER Some versions of the dispaly have the polarity of the LED pins "A" and "K" reversed.
